# Fritzing sketch 10-AnalogInputWithoutPotentiometer (saved by Fritzing 1.0.2b)
breadboards: 1

parts:
  Part1 = Arduino Uno (Rev3)
  R1 = Resistor [tolerance=±5% resistance=10k package="0805 [SMD]"]
  R2 = Resistor [tolerance=±5% resistance=10k package="0805 [SMD]"]

nets:
  N1: Part1.A0, R1.Pin_0, R2.Pin_1
  N2: Part1.GND, R2.Pin_0
  N3: Part1.5V, R1.Pin_1
