# Fritzing sketch 11-WithPotentiometer (saved by Fritzing 1.0.2b)
breadboards: 1

parts:
  Part2 = Arduino Uno (Rev3)
  R1 = Rotary Potentiometer (Small) [maximum_resistance=100kΩ knob_status=50% power=0.5W package=THT]

nets:
  N1: Part2.A0, R1.wiper
  N2: Part2.GND, R1.leg1
  N3: Part2.5V, R1.leg2
