# Fritzing sketch 12-PotentiometerVelocityControl (saved by Fritzing 1.0.2b)
breadboards: 1

parts:
  Part3 = Arduino Uno (Rev3)
  R2 = Rotary Potentiometer (Small) [maximum_resistance=100kΩ knob_status=50% power=0.5W package=THT]
  LED1 = smd LED [color="Red (633nm)" package="0805 [SMD]"]
  R3 = Resistor [tolerance=±5% resistance=220 package="2010 [SMD]"]

nets:
  N1: Part3.A0, R2.wiper
  N2: Part3.D9_PWM, LED1.anode
  N3: Part3.5V, R2.leg2
  N4: Part3.GND, R2.leg1, R3.Pin_0
  N5: LED1.cathode, R3.Pin_1
