# Fritzing sketch 15-BuzzerWithPotentiometer (saved by Fritzing 1.0.2b)
breadboards: 1

parts:
  R2 = Resistor [tolerance=±5% power=0.25W resistance=220 package=THT]
  R3 = Rotary Potentiometer (Small) [maximum_resistance=10kΩ knob_status=50% power=0.5W package=THT]
  LED1 = smd LED [color="Red (633nm)" package="0805 [SMD]"]
  R4 = Resistor [tolerance=±5% power=0.25W resistance=220 package=THT]
  Part1 = Arduino Uno (Rev3)
  J1 = Piezo Speaker

nets:
  N1: R2.Pin_0, R3.leg1, R4.Pin_0, Part1.GND
  N2: R2.Pin_1, J1.pin1
  N3: R3.wiper, Part1.A0
  N4: R3.leg2, Part1.5V
  N5: LED1.cathode, R4.Pin_1
  N6: LED1.anode, Part1.D9_PWM
  N7: Part1.D11_PWM/MOSI, J1.pin2
