# Fritzing sketch LCD (saved by Fritzing 1.0.2b)

parts:
  Part1 = Arduino Uno (Rev3)
  Part2 = LCD1602-I2C

nets:
  N1: Part1.A4/SDA, Part2.SDA
  N2: Part1.A5/SCL, Part2.SCL
  GND: Part1.GND, Part2.GND
  5V: Part1.5V, Part2.VCC

custom parts:
  LCD1602-I2C: A standard character display, usually with 2x16 characters. Comes in many colors with LCM1602 IIC attached.
