# Fritzing sketch 2-First LED Interaction (saved by Fritzing 1.0.2b)
breadboards: 1

parts:
  LED1 = LED - 5mm [color="Red (633nm)" current=0.030A package="5 mm [THT]"]
  R1 = Resistor [tolerance=±5% power=0.25W resistance=330 package=THT]
  VCC1 = Battery block 9V
  S1 = Pushbutton [package="[THT]"]
  L298N1 = L298N DC motor driver  # not connected

nets:
  N1: LED1.cathode, R1.Pin_0
  N2: LED1.anode, S1.Pin_3, S1.Pin_4
  N3: R1.Pin_1, VCC1.-
  N4: VCC1.+, S1.Pin_1, S1.Pin_2

notes:
  Led Resistor

custom parts:
  L298N DC motor driver: 2x DC motor driver with 78M05 positive voltage regulator (7..35 V) L298N: max 46 V, 2 A Set 5 V Enable jumper to enable 5 V regultor (needed for the L298N) and +5 V output at screw terminal or supply external +5 V at screw terminal Set ENA and/or ENB to +5 V to enable motor permanently or supply ENA and/or ENB with PWM signal IN1 and IN2 set rotation directory for motor A (OUT1/OUT2) IN2 and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
