# Fritzing sketch Untitled Sketch (saved by Fritzing 1.0.2b)
breadboards: 1

parts:
  Part1 = Arduino Uno (Rev3)
  T1 = LM35 Temperature Sensor [package="TO92 [THT]"]
  Part2 = LCD1602-I2C

nets:
  N1: Part1.A0, T1.Vout
  GND: Part1.GND, Part2.GND
  N2: Part1.A4/SDA, Part2.SCL
  N3: Part1.A5/SCL, Part2.SDA
  5V: Part1.5V, Part2.VCC

custom parts:
  LCD1602-I2C: A standard character display, usually with 2x16 characters. Comes in many colors with LCM1602 IIC attached.
