# Fritzing sketch Untitled Sketch (saved by Fritzing 1.0.2b)
breadboards: 1

parts:
  Part3 = Arduino Uno (Rev3)
  T2 = LM35 Temperature Sensor [package="TO92 [THT]"]
  Part4 = LCD1602-I2C
  LED1 = LED - 5mm [color="Red (633nm)" current=0.030A package="5 mm [THT]"]
  R1 = Resistor [tolerance=±5% power=0.25W resistance=220 package=THT]
  J1 = Piezo Speaker

nets:
  N1: Part3.A0, T2.Vout
  N2: Part3.D11_PWM/MOSI, J1.pin2
  GND: Part3.GND, Part4.GND, J1.pin1
  N3: Part3.A4/SDA, Part4.SCL
  N4: Part3.A5/SCL, Part4.SDA
  N5: Part3.D2, LED1.anode
  5V: Part3.5V, Part4.VCC
  N6: T2.GND, R1.Pin_0
  N7: LED1.cathode, R1.Pin_1

custom parts:
  LCD1602-I2C: A standard character display, usually with 2x16 characters. Comes in many colors with LCM1602 IIC attached.
