# Fritzing sketch Untitled Sketch (saved by Fritzing 1.0.2b)
breadboards: 1

parts:
  Part2 = Arduino Uno (Rev3)
  R3 = Photocell (LDR) [power=0.25W dark_resistance_@0.01lx=300kΩ light_resistance_@100lx=400Ω luminance=10lx package=THT]
  R4 = Resistor [tolerance=±5% power=0.25W resistance=220 package=THT]
  LED1 = LED - 5mm [color="Red (633nm)" current=0.030A package="5 mm [THT]"]
  R5 = Resistor [tolerance=±5% power=0.25W resistance=220 package=THT]

nets:
  N1: Part2.A0, R3.pin_0, R4.Pin_1
  N2: Part2.D2, LED1.anode
  N3: Part2.5V, R3.pin_1
  N4: Part2.GND, R4.Pin_0, R5.Pin_0
  N5: LED1.cathode, R5.Pin_1
