# Fritzing sketch Untitled Sketch (saved by Fritzing 1.0.2b)

parts:
  Part1 = Arduino Uno (Rev3)
  TCS1 = TCS3200

nets:
  N1: Part1.D8, TCS1.S1
  N2: Part1.D9_PWM, TCS1.S0
  N3: Part1.D10_PWM/SS, TCS1.S2
  N4: Part1.D11_PWM/MOSI, TCS1.S3
  N5: Part1.D12/MISO, TCS1.OUT
  5V: Part1.5V, TCS1.VCC
  GND: Part1.GND, TCS1.GND

custom parts:
  TCS3200: COLOR SENSING TCS3200
