# Fritzing sketch Untitled Sketch 3 (saved by Fritzing 1.0.2b)
breadboards: 1

parts:
  Part3 = Arduino Uno (Rev3)
  Part4 = HC-SR501 Body Sensor Module
  LED1 = LED - 5mm [color="Red (633nm)" current=0.030A package="5 mm [THT]"]
  J1 = Piezo Speaker
  R1 = Resistor [tolerance=±5% resistance=220 package="0805 [SMD]"]
  R2 = Resistor [tolerance=±5% resistance=220 package="0805 [SMD]"]

nets:
  N1: Part3.D8, LED1.anode
  N2: Part3.D9_PWM, Part4.OUT
  N3: Part3.D7, J1.pin2
  5V: Part3.5V, Part4.VCC
  GND: Part3.GND, Part4.GND, R1.Pin_0, R2.Pin_0
  N4: LED1.cathode, R1.Pin_1
  N5: J1.pin1, R2.Pin_1

custom parts:
  HC-SR501 Body Sensor Module: Pyroelectric Infrared PIR Motion Sensor Detector Module
