# Fritzing sketch Untitled Sketch (saved by Fritzing 1.0.2b)

parts:
  KY-008_Laserdiode1 = Laser [part_number=1219301 package=keys]
  Part1 = Arduino Uno (Rev3)

nets:
  N1: KY-008_Laserdiode1.connector0pin, Part1.D7
  N2: KY-008_Laserdiode1.connector1pin, Part1.5V
  N3: KY-008_Laserdiode1.connector2pin, Part1.GND

custom parts:
  Laser: KEYES KY-008 650nm Laser Transmitter Module
