# Fritzing sketch Untitled Sketch (saved by Fritzing 1.0.2b)
breadboards: 1

parts:
  KY-008_Laserdiode1 = Laser [part_number=1219301 package=keys]
  R1 = Photocell (LDR) [power=0.25W dark_resistance_@0.01lx=300kΩ light_resistance_@100lx=400Ω luminance=10lx package=THT]
  Part1 = Arduino Uno (Rev3)
  R2 = Resistor [tolerance=±5% resistance=10k package="2010 [SMD]"]

nets:
  N1: KY-008_Laserdiode1.connector0pin, Part1.D7
  N2: KY-008_Laserdiode1.connector1pin, R1.pin_1, Part1.5V
  N3: KY-008_Laserdiode1.connector2pin, Part1.GND, R2.Pin_0
  N4: R1.pin_0, Part1.A0, R2.Pin_1

custom parts:
  Laser: KEYES KY-008 650nm Laser Transmitter Module
