# Fritzing sketch 3-FLIP FLOP (saved by Fritzing 1.0.2b)
breadboards: 1

parts:
  R1 = Resistor [tolerance=±5% power=0.25W resistance=220 package=THT]
  R2 = Resistor [tolerance=±5% power=0.25W resistance=220 package=THT]
  Part1 = Arduino Uno (Rev3)
  LED1 = LED - 5mm [color="Red (633nm)" current=0.030A package="5 mm [THT]"]
  LED2 = LED - 5mm [color="Blue (505nm)" current=0.030A package="5 mm [THT]"]

nets:
  N1: R1.Pin_0, R2.Pin_0, Part1.GND
  N2: R1.Pin_1, LED1.cathode
  N3: R2.Pin_1, LED2.cathode
  N4: Part1.D9_PWM, LED2.anode
  N5: Part1.D10_PWM/SS, LED1.anode
