# Fritzing sketch Untitled Sketch (saved by Fritzing 1.0.2b)

parts:
  Part1 = Arduino Uno (Rev3)
  M3 = fc-51 [package=THT]

nets:
  N1: Part1.D10_PWM/SS, M3.pin1
  N2: Part1.5V, M3.pin3
  N3: Part1.GND, M3.pin2
