# Fritzing sketch Untitled Sketch (saved by Fritzing 1.0.2b)
breadboards: 1

parts:
  Part1 = Arduino Uno (Rev3)
  FC-1 = Sound Sensor
  LED1 = LED - 5mm [color="Red (633nm)" current=0.030A package="5 mm [THT]"]
  R1 = Resistor [tolerance=±5% power=0.25W resistance=220 package=THT]

nets:
  N1: Part1.D8, FC-1.OUT
  N2: Part1.D9_PWM, LED1.anode
  GND: Part1.GND, FC-1.GND, R1.Pin_1
  5V: Part1.5V, FC-1.VCC
  N3: LED1.cathode, R1.Pin_0
