# Fritzing sketch Untitled Sketch (saved by Fritzing 1.0.2b)

parts:
  SD_card_module1 = SD Card Module
  Part1 = Arduino Uno (Rev3)
  SPKR1 = Loudspeaker

nets:
  N1: SD_card_module1.+3.3, Part1.3V3
  N2: SD_card_module1.+5, Part1.5V
  N3: SD_card_module1.CS, Part1.D4
  N4: SD_card_module1.MOSI, Part1.D11_PWM/MOSI
  N5: SD_card_module1.SCK, Part1.D13/SCK
  N6: SD_card_module1.MISO, Part1.D12/MISO
  GND: SD_card_module1.GND, Part1.GND, SPKR1.pin1
  N7: Part1.D9_PWM, SPKR1.pin2

custom parts:
  SD Card Module: SD Card Module Slot Socket Reader For Arduino ARM MCU
