# Fritzing sketch Untitled Sketch (saved by Fritzing 1.0.2b)
breadboards: 1

parts:
  Part1 = MQ-4
  Part2 = Arduino Uno (Rev3)
  R1 = Resistor [tolerance=±5% power=0.25W resistance=220 package=THT]
  LED1 = RGB LED (com. cathode, rgb) [color="Red (633nm)" current=0.030A package="5 mm [THT]"]
  R2 = Resistor [tolerance=±5% power=0.25W resistance=220 package=THT]
  R3 = Resistor [tolerance=±5% power=0.25W resistance=220 package=THT]
  J1 = Piezo Speaker

nets:
  VCC: Part1.VCC, Part2.5V
  GND: Part1.GND, Part2.GND, LED1.common_cathode, J1.pin1
  N1: Part1.AO, Part2.A0
  N2: Part2.D9_PWM, R1.Pin_0
  N3: Part2.D10_PWM/SS, R2.Pin_0
  N4: Part2.D11_PWM/MOSI, R3.Pin_0
  N5: Part2.D13/SCK, J1.pin2
  N6: R1.Pin_1, LED1.blue_anode
  N7: LED1.red_anode, R3.Pin_1
  N8: LED1.green_anode, R2.Pin_1
