# Fritzing sketch Untitled Sketch (saved by Fritzing 1.0.2b)
breadboards: 1

parts:
  Part1 = Arduino Uno (Rev3)
  M1 = gy9250

nets:
  N1: Part1.A4/SDA, M1.pin4
  N2: Part1.A5/SCL, M1.pin3
  N3: Part1.5V, M1.pin1
  N4: Part1.GND, M1.pin2

custom parts:
  gy9250: MPU-9250 module (three-axis gyroscope + three-axis acceleration + three-axis magnetic field). The generic model from ebay et. al. rather than the Sparkfun version.
