# Fritzing sketch 6-RGB (saved by Fritzing 1.0.2b)
breadboards: 1

parts:
  Part1 = Arduino Uno (Rev3)
  R1 = Resistor [tolerance=±5% resistance=220 package="0603 [SMD]"]
  R2 = Resistor [tolerance=±5% resistance=220 package="0603 [SMD]"]
  R3 = Resistor [tolerance=±5% resistance=220 package="0603 [SMD]"]
  LED1 = RGB LED - (4 legs) [color="Red (633nm)" current=0.030A package="5 mm [THT]"]

nets:
  N1: Part1.5V, LED1.common_anode
  N2: R1.Pin_0, LED1.green_cathode
  N3: R2.Pin_0, LED1.red_cathode
  N4: R3.Pin_0, LED1.blue_cathode
