# Fritzing sketch 7-PullUPDOWN (saved by Fritzing 1.0.2b)

parts:
  Part1 = Arduino Uno (Rev3)
  S1 = Pushbutton [package=THT]
  R1 = Resistor [tolerance=±5% power=0.25W resistance=220 package=THT]
  Part2 = Arduino Uno (Rev3)
  S2 = Pushbutton [package=THT]
  R2 = Resistor [tolerance=±5% power=0.25W resistance=220 package=THT]
  Part3 = Arduino Uno (Rev3)
  S3 = Toggle Switch [package=THT]

nets:
  N1: Part1.D13/SCK, S1.leg0, R1.Pin_0
  N2: Part1.GND, S1.leg1
  N3: Part1.5V, R1.Pin_1
  N4: Part2.D13/SCK, S2.leg1, R2.Pin_1
  N5: Part2.GND, R2.Pin_0
  N6: Part2.5V, S2.leg0
  N7: Part3.D13/SCK, S3.COM
  N8: Part3.GND, S3.L1
  N9: Part3.5V, S3.L2

notes:
  Pull Up Resistor with push button
  Pull Down Resistor with push button
  Toggleswitch key connection
