# Fritzing sketch 9-2buttonPullOnBreadboard (saved by Fritzing 1.0.2b)
breadboards: 1

parts:
  Part1 = Arduino Uno (Rev3)
  R1 = Resistor [tolerance=±5% power=0.25W resistance=10k package=THT]
  S1 = Pushbutton [package="[THT]"]
  R2 = Resistor [tolerance=±5% power=0.25W resistance=33 package=THT]
  LED1 = LED - 5mm [color="Red (633nm)" current=0.030A package="5 mm [THT]"]
  S2 = Pushbutton [package="[THT]"]
  R3 = Resistor [tolerance=±5% power=0.25W resistance=10k package=THT]

nets:
  N1: Part1.D9_PWM, LED1.anode
  N2: Part1.D10_PWM/SS, R1.Pin_0, S1.Pin_1, S1.Pin_2
  N3: Part1.D11_PWM/MOSI, S2.Pin_1, S2.Pin_2, R3.Pin_0
  N4: R1.Pin_1, R2.Pin_0, R3.Pin_1
  N5: S1.Pin_3, S1.Pin_4, S2.Pin_3, S2.Pin_4
  N6: R2.Pin_1, LED1.cathode

notes:
  Resistor connection with 2 button pull down connection
